// Logisim project Lezione 3 - Esercizio 1.circ as structural Verilog: 1 circuit, main circuit main
module main (
  input  A,
  input  C,
  input  B,
  output out_4,
  output out_5,
  output out_6,
  output out_7
);

  not not_1 (out_4, A);
  or or_1 (out_5, out_4, C);
  or or_2 (out_7, A, B);
  and and_1 (out_6, out_5, out_7);
endmodule
