// Logisim project Lezione 3 - Esercizio 2.circ as structural Verilog: 1 circuit, main circuit main
module main (
  input  A,
  input  B,
  output out_3
);

  wire and_1_out, and_2_out, not_1_out, not_2_out, or_1_out, xnor_1_out;

  not not_1 (not_1_out, A);
  not not_2 (not_2_out, B);
  and and_1 (and_1_out, A, B);
  and and_2 (and_2_out, not_1_out, not_2_out);
  or or_1 (or_1_out, and_1_out, and_2_out);
  xnor xnor_1 (xnor_1_out, B, A);
  xnor xnor_2 (out_3, or_1_out, xnor_1_out);

  // Notes on the sheet:
  //   Porta XNOR
  //   Test di uguaglianza tra porta XNOR e implementazione con porte semplici
endmodule
