// Logisim project Lezione 3 - Esercizio 3.circ as structural Verilog: 1 circuit, main circuit main
module main (
  input  A,
  input  B,
  input  C,
  output out_4
);

  wire not_1_out, not_2_out, not_3_out, or_1_out;

  not not_1 (not_1_out, A);
  not not_2 (not_2_out, C);
  or or_1 (or_1_out, B, not_2_out);
  not not_3 (not_3_out, or_1_out);
  or or_2 (out_4, not_1_out, not_3_out);
endmodule
