// Logisim project Lezione 3 - Esercizio 5.circ as structural Verilog: 1 circuit, main circuit main
module main (
  input  A,
  input  B,
  input  C,
  output out_4
);

  wire and_1_out, nand_1_out, nand_2_out, nand_3_out, nand_4_out, nand_5_out, nand_6_out, nand_7_out,
       nand_8_out, not_1_out, not_2_out;

  not not_1 (not_1_out, A);
  not not_2 (not_2_out, B);
  nand nand_1 (nand_1_out, A, A);
  nand nand_2 (nand_2_out, B, B);
  nand nand_3 (nand_3_out, C, C);
  and and_1 (and_1_out, not_1_out, not_2_out);
  nand nand_4 (nand_4_out, nand_1_out, nand_2_out);
  nand nand_5 (nand_5_out, nand_4_out, nand_4_out);
  nand nand_6 (nand_6_out, B, nand_3_out);
  nand nand_7 (nand_7_out, nand_5_out, nand_6_out);
  nand nand_8 (nand_8_out, nand_7_out, nand_7_out);
  xnor xnor_1 (out_4, nand_8_out, and_1_out);

  // Notes on the sheet:
  //   !C
  //   !A
  //   !B
  //   A OR B
  //   A NOR B
  //   C OR !B
  //   (A NOR B)(C+!B)
endmodule
