// Logisim project Lezione 5 - Esercizio 1.circ as structural Verilog: 1 circuit, main circuit Decodificatore a 2 vie
module Decodificatore_a_2_vie (
  input  A,
  input  B,
  output out_3,
  output out_4,
  output out_5,
  output out_6
);

  and and_1 (out_3, ~A, ~B);  // AND_Gate
  and and_2 (out_4, ~A, B);  // AND_Gate
  and and_3 (out_5, A, ~B);  // AND_Gate
  and and_4 (out_6, A, B);
endmodule
