// Logisim project Lezione 5 - Esercizio 2-4.circ as structural Verilog: 2 circuits, main circuit Half Adder
module Half_Adder (
  input  A,
  input  B,
  output out_3,
  output out_4
);

  xor xor_1 (out_3, A, B);
  and and_1 (out_4, A, B);

  // Notes on the sheet:
  //   Half Adder a 1 bit
endmodule

module Addizionatore_a_4_bit (
  input  [3:0] A,
  input  [3:0] B,
  output [4:0] out_3
);

  wire adder_1_cout, adder_2_cout, half_adder_1_out_4;

  Half_Adder half_adder_1 (.A(A[0]), .B(B[0]), .out_3(out_3[0]), .out_4(half_adder_1_out_4));
  Adder #(.width(1)) adder_1 (.a(A[1]), .b(B[1]), .out(out_3[1]), .cin(half_adder_1_out_4), .cout(adder_1_cout));
  Adder #(.width(1)) adder_2 (.a(A[2]), .b(B[2]), .out(out_3[2]), .cin(adder_1_cout), .cout(adder_2_cout));
  Adder #(.width(1)) adder_3 (.a(A[3]), .b(B[3]), .out(out_3[3]), .cin(adder_2_cout), .cout(out_3[4]));
endmodule
