// Logisim project Lezione 5 - Esercizio 2.circ as structural Verilog: 1 circuit, main circuit main
module main (
  input  A,
  input  B,
  output out_3,
  output out_4
);

  xor xor_1 (out_3, A, B);
  and and_1 (out_4, A, B);

  // Notes on the sheet:
  //   Half Adder a 1 bit
endmodule
