// Logisim project Lezione 5 - Esercizio 5.circ as structural Verilog: 1 circuit, main circuit main
module main (
  input  [3:0] X,
  input  [3:0] in_2,
  output [3:0] out_3,
  output out_4
);

  wire [3:0] not_1_out;

  not not_1 (not_1_out[0], X[0]);
  not not_2 (not_1_out[1], X[1]);
  not not_3 (not_1_out[2], X[2]);
  not not_4 (not_1_out[3], X[3]);
  Adder #(.width(4)) adder_1 (.a(not_1_out), .b(in_2), .out(out_3), .cout(out_4));  // open: cin

  // Notes on the sheet:
  //   Dato un numero binario in input, fornire -X in CA2
endmodule
