// Logisim project Lezione 5 - Esercizio 6.circ as structural Verilog: 1 circuit, main circuit main
module main (
  input  Interti_B,
  input  [3:0] A,
  input  [3:0] B,
  output [3:0] out_4,
  output out_5,
  output [3:0] out_6
);

  wire [3:0] not_1_out;

  not not_1 (not_1_out[0], B[0]);
  not not_2 (not_1_out[1], B[1]);
  not not_3 (not_1_out[2], B[2]);
  not not_4 (not_1_out[3], B[3]);
  Multiplexer #(.width(4), .enable("false")) multiplexer_1 (.in0(B), .in1(not_1_out), .out(out_6), .sel(Interti_B));
  Adder #(.width(4)) adder_1 (.a(A), .b(out_6), .out(out_4), .cin(Interti_B), .cout(out_5));
endmodule
