// Logisim project Lezione 5 Dicembre.circ as structural Verilog: 5 circuits, main circuit main
module main (
  input  [3:0] in_1,
  input  in_2
);

  wire button_1_out;
  wire [3:0] linear_feedback_shift_register_1_out_4;

  Hex_Digit_Display hex_digit_display_1 (.value(linear_feedback_shift_register_1_out_4));  // open: dp
  Button button_1 (.out(button_1_out));
  Linear_Feedback_Shift_Register linear_feedback_shift_register_1 (
    .Seed(in_1), .out_4(linear_feedback_shift_register_1_out_4), .Clock(button_1_out), .LOAD(in_2));
endmodule

module Output (
  input  [2:0] in_1,
  output [2:0] out_2
);


  assign out_2 = in_1;
endmodule

module Next (
  input  [2:0] in_1,
  output [2:0] out_2
);

  wire and_1_out;

  not not_1 (out_2[0], in_1[0]);
  xor xor_1 (out_2[1], in_1[0], in_1[1]);
  and and_1 (and_1_out, in_1[0], in_1[1]);
  xor xor_2 (out_2[2], and_1_out, in_1[2]);
endmodule

module ContatoreModulo8 (
  input  in_1
);

  wire clock_1_out, undriven;
  wire [2:0] d_ff_1_q, next_1_out_2;

  Clock clock_1 (.out(clock_1_out));
  D_Flip_Flop d_ff_1 (
    .clk(clock_1_out), .D(next_1_out_2[0]), .Q(d_ff_1_q[0]), .reset(undriven));  // open: Qn, preset, en
  D_Flip_Flop d_ff_2 (.clk(clock_1_out), .D(next_1_out_2[1]), .Q(d_ff_1_q[1]));  // open: Qn, preset, en, reset
  D_Flip_Flop d_ff_3 (.clk(clock_1_out), .D(next_1_out_2[2]), .Q(d_ff_1_q[2]));  // open: Qn, preset, en, reset
  Next next_1 (.in_1(d_ff_1_q), .out_2(next_1_out_2));
  Hex_Digit_Display hex_digit_display_1 (.value({in_1, d_ff_1_q}));  // open: dp
endmodule

module Linear_Feedback_Shift_Register (
  input  [3:0] Seed,
  input  Clock,
  input  LOAD,
  output [3:0] out_4
);

  wire multiplexer_1_out, multiplexer_2_out, multiplexer_3_out, multiplexer_4_out, xor_1_out;

  Multiplexer #(.enable("false")) multiplexer_1 (.in0(xor_1_out), .in1(Seed[0]), .out(multiplexer_1_out), .sel(LOAD));
  D_Flip_Flop d_ff_1 (.clk(Clock), .D(multiplexer_1_out), .Q(out_4[3]));  // open: Qn, preset, en, reset
  Hex_Digit_Display hex_digit_display_1 (.value(out_4));  // open: dp
  xor xor_1 (xor_1_out, out_4[0], out_4[1]);
  Multiplexer #(.enable("false")) multiplexer_2 (.in0(out_4[3]), .in1(Seed[1]), .out(multiplexer_2_out), .sel(LOAD));
  D_Flip_Flop d_ff_2 (.clk(Clock), .D(multiplexer_2_out), .Q(out_4[2]));  // open: Qn, preset, en, reset
  Multiplexer #(.enable("false")) multiplexer_3 (.in0(out_4[2]), .in1(Seed[2]), .out(multiplexer_3_out), .sel(LOAD));
  D_Flip_Flop d_ff_3 (.clk(Clock), .D(multiplexer_3_out), .Q(out_4[1]));  // open: Qn, preset, en, reset
  Multiplexer #(.enable("false")) multiplexer_4 (.in0(out_4[1]), .in1(Seed[3]), .out(multiplexer_4_out), .sel(LOAD));
  D_Flip_Flop d_ff_4 (.clk(Clock), .D(multiplexer_4_out), .Q(out_4[0]));  // open: Qn, preset, en, reset
endmodule
