// Logisim project Lezione 6 - Esercizio 1.circ as structural Verilog: 1 circuit, main circuit main
module main (
  input  [2:0] A,
  input  [2:0] B,
  output [5:0] out_3
);

  wire adder_1_cout, adder_2_cout, adder_2_out, adder_4_cout, and_2_out, and_3_out, and_4_out, and_5_out,
       and_6_out, and_7_out, and_8_out, and_9_out;

  and and_1 (out_3[0], B[0], A[0]);
  and and_2 (and_2_out, B[0], A[2]);
  and and_3 (and_3_out, B[0], A[1]);
  and and_4 (and_4_out, B[1], A[0]);
  and and_5 (and_5_out, B[1], A[2]);
  and and_6 (and_6_out, B[1], A[1]);
  Adder #(.width(1)) adder_1 (.a(and_3_out), .b(and_4_out), .out(out_3[1]), .cout(adder_1_cout));  // open: cin
  Adder #(.width(1)) adder_2 (.a(and_2_out), .b(and_6_out), .out(adder_2_out), .cin(adder_1_cout), .cout(adder_2_cout));
  and and_7 (and_7_out, B[2], A[0]);
  Adder #(.width(1)) adder_3 (.a(adder_2_out), .b(and_7_out), .out(out_3[2]));  // open: cin, cout
  Adder #(.width(1)) adder_4 (.a(and_5_out), .b(and_9_out), .out(out_3[3]), .cin(adder_2_cout), .cout(adder_4_cout));
  Adder #(.width(1)) adder_5 (.a(and_8_out), .b(adder_4_cout), .out(out_3[4]), .cout(out_3[5]));  // open: cin
  and and_8 (and_8_out, B[2], A[2]);
  and and_9 (and_9_out, B[2], A[1]);
endmodule
