// Logisim project Lezione 7 - Esercizio 1.circ as structural Verilog: 4 circuits, main circuit Bistabile SR
module Bistabile_SR (
  input  A,
  input  B,
  output out_3,
  output out_4
);

  nor nor_1 (out_3, A, out_4);
  nor nor_2 (out_4, out_3, B);
endmodule

module Bistabile_SR_PACK (
  input  RESET,
  input  CLOCK,
  input  SET,
  output out_4,
  output out_5
);

  wire and_1_out, and_2_out;

  and and_1 (and_1_out, RESET, CLOCK);
  and and_2 (and_2_out, CLOCK, SET);
  Bistabile_SR bistabile_sr_1 (.A(and_1_out), .B(and_2_out), .out_3(out_4), .out_4(out_5));

  // Notes on the sheet:
  //   Reset
  //   Set
endmodule

module Latch_D_Sincrono (
  input  D,
  input  CLOCK,
  output Q,
  output nQ
);

  wire not_1_out;

  not not_1 (not_1_out, D);
  Bistabile_SR_PACK bistabile_sr_pack_1 (.RESET(not_1_out), .CLOCK(CLOCK), .SET(not_1_out), .out_4(Q), .out_5(nQ));
endmodule

module Bistabile_SR_Sincrono (
  input  A,
  input  B,
  output out_3,
  output out_4
);

  wire and_1_out, and_2_out, clock_1_out;

  Clock clock_1 (.out(clock_1_out));
  and and_1 (and_1_out, A, clock_1_out);
  and and_2 (and_2_out, clock_1_out, B);
  nor nor_1 (out_3, and_1_out, out_4);
  nor nor_2 (out_4, out_3, and_2_out);
endmodule
