// Logisim project RiconosciStringa010e101 V1.circ as structural Verilog: 3 circuits, main circuit main
module main (
  input  in_1,
  output out_2
);

  wire clock_1_out, d_ff_1_q, d_ff_2_q, d_ff_3_q, nextstatefunction_1_b0_prime, nextstatefunction_1_b1_prime,
       nextstatefunction_1_b2_prime;

  Clock clock_1 (.out(clock_1_out));
  NextStateFunction nextstatefunction_1 (
    .x(in_1), .b0(d_ff_1_q), .b1(d_ff_2_q), .b2(d_ff_3_q), .b0_prime(nextstatefunction_1_b0_prime),
    .b1_prime(nextstatefunction_1_b1_prime), .b2_prime(nextstatefunction_1_b2_prime));
  D_Flip_Flop d_ff_1 (
    .clk(clock_1_out), .D(nextstatefunction_1_b0_prime), .Q(d_ff_1_q));  // open: Qn, preset, en, reset
  D_Flip_Flop d_ff_2 (
    .clk(clock_1_out), .D(nextstatefunction_1_b1_prime), .Q(d_ff_2_q));  // open: Qn, preset, en, reset
  D_Flip_Flop d_ff_3 (
    .clk(clock_1_out), .D(nextstatefunction_1_b2_prime), .Q(d_ff_3_q));  // open: Qn, preset, en, reset
  Output output_1 (.in_1(d_ff_1_q), .in_2(d_ff_2_q), .in_3(d_ff_3_q), .out_4(out_2));
endmodule

module Output (
  input  in_1,
  input  in_2,
  input  in_3,
  output out_4
);

  wire and_1_out, and_2_out, not_1_out, not_2_out, not_3_out;

  not not_1 (not_1_out, in_1);
  not not_2 (not_2_out, in_3);
  not not_3 (not_3_out, in_2);
  and and_1 (and_1_out, not_1_out, in_2, not_2_out);
  and and_2 (and_2_out, in_1, not_3_out, in_3);
  or or_1 (out_4, and_1_out, and_2_out);
endmodule

module NextStateFunction (
  input  x,
  input  b0,
  input  b1,
  input  b2,
  output b0_prime,
  output b1_prime,
  output b2_prime
);


  assign b0_prime = x;
  assign b1_prime = b0;
  assign b2_prime = b1;
  // also tied to GND on the sheet: b2
endmodule
