// Logisim project Riconoscitore Stringa 010 e 101 V2 IMPROVED.circ as structural Verilog: 3 circuits, main circuit Output
module Output (
  input  S0,
  input  S1,
  input  S2,
  output out_4
);

  wire and_1_out, and_2_out;

  and and_1 (and_1_out, S0, ~S1, S2);  // AND_Gate
  or or_1 (out_4, and_1_out, and_2_out);
  and and_2 (and_2_out, ~S0, S1, ~S2);  // AND_Gate
endmodule

module NextState (
  input  INPUT,
  input  S0,
  input  S1,
  input  S2,
  output S0_prime,
  output S1_prime,
  output S2_prime
);


  assign S0_prime = INPUT;
  assign S1_prime = S0;
  assign S2_prime = S1;
  // also tied to GND on the sheet: S2

  // Notes on the sheet:
  //   (inutilizzato)
endmodule

module RiconoscitoreStringa (
  input  Input,
  output Output
);

  wire clock_1_out, d_ff_1_q, d_ff_2_q, d_ff_3_q, nextstate_1_s0_prime, nextstate_1_s1_prime,
       nextstate_1_s2_prime;

  Output output_1 (.S0(d_ff_1_q), .S1(d_ff_2_q), .S2(d_ff_3_q), .out_4(Output));
  NextState nextstate_1 (
    .INPUT(Input), .S0(d_ff_1_q), .S1(d_ff_2_q), .S2(d_ff_3_q), .S0_prime(nextstate_1_s0_prime),
    .S1_prime(nextstate_1_s1_prime), .S2_prime(nextstate_1_s2_prime));
  Clock clock_1 (.out(clock_1_out));
  D_Flip_Flop d_ff_1 (.clk(clock_1_out), .D(nextstate_1_s0_prime), .Q(d_ff_1_q));  // open: Qn, preset, en, reset
  D_Flip_Flop d_ff_2 (.clk(clock_1_out), .D(nextstate_1_s1_prime), .Q(d_ff_2_q));  // open: Qn, preset, en, reset
  D_Flip_Flop d_ff_3 (.clk(clock_1_out), .D(nextstate_1_s2_prime), .Q(d_ff_3_q));  // open: Qn, preset, en, reset

  // Notes on the sheet:
  //   Current state
  //   Next state
  //   Current state
  //   Current state
endmodule
