// Logisim project Sommatore 4 bit.circ as structural Verilog: 3 circuits, main circuit output
module \output  (
  input  S0,
  output OUTPUT
);


  assign OUTPUT = S0;
endmodule

module NextState (
  input  S0,
  input  S1,
  input  I0,
  input  I1,
  output S0_prime,
  output S1_prime
);

  wire and_1_out, and_2_out, xor_1_out;

  xor xor_1 (xor_1_out, I0, I1);
  xor xor_2 (S0_prime, S1, xor_1_out);
  and and_1 (and_1_out, xor_1_out, S1);
  and and_2 (and_2_out, I0, I1);
  or or_1 (S1_prime, and_1_out, and_2_out);
  // also tied to GND on the sheet: S0
endmodule

module Sommatore (
  input  I1,
  input  I0,
  output Output
);

  wire clock_1_out, d_ff_1_q, d_ff_2_q, nextstate_1_s0_prime, nextstate_1_s1_prime;

  \output  output_1 (.S0(d_ff_1_q), .OUTPUT(Output));
  NextState nextstate_1 (
    .S0(d_ff_1_q), .S1(d_ff_2_q), .I0(I0), .I1(I1), .S0_prime(nextstate_1_s0_prime),
    .S1_prime(nextstate_1_s1_prime));
  Clock clock_1 (.out(clock_1_out));
  D_Flip_Flop d_ff_1 (.clk(clock_1_out), .D(nextstate_1_s0_prime), .Q(d_ff_1_q));  // open: Qn, preset, en, reset
  D_Flip_Flop d_ff_2 (.clk(clock_1_out), .D(nextstate_1_s1_prime), .Q(d_ff_2_q));  // open: Qn, preset, en, reset

  // Notes on the sheet:
  //   Current State
  //   Output
  //   Next state
  //   Current state
endmodule
