// Logisim project Tema esame 20-09-2023  - Esercizio 2.circ as structural Verilog: 3 circuits, main circuit Output
module Output (
  input  S0,
  input  S1,
  output Output
);


  assign Output = S1;
  // also tied to GND on the sheet: S0
endmodule

module NextState (
  input  Input,
  input  S0,
  input  S1,
  output S0Next,
  output S1Next
);

  wire and_1_out, and_2_out, and_3_out, and_4_out;

  and and_1 (and_1_out, Input, ~S0, ~S1);  // AND_Gate
  and and_2 (and_2_out, S1, ~Input);  // AND_Gate
  and and_3 (and_3_out, S1, Input);
  and and_4 (and_4_out, S0, Input);
  or or_1 (S0Next, and_1_out, and_2_out);
  or or_2 (S1Next, and_3_out, and_4_out);
endmodule

module Esercizio_2_Prova_Tema_Esame (
  input  Input,
  output Output
);

  wire clock_1_out, d_ff_1_q, d_ff_2_q, nextstate_1_s0next, nextstate_1_s1next;

  Output output_1 (.S0(d_ff_1_q), .S1(d_ff_2_q), .Output(Output));
  NextState nextstate_1 (
    .Input(Input), .S0(d_ff_1_q), .S1(d_ff_2_q), .S0Next(nextstate_1_s0next), .S1Next(nextstate_1_s1next));
  Clock clock_1 (.out(clock_1_out));
  D_Flip_Flop d_ff_1 (.clk(clock_1_out), .D(nextstate_1_s0next), .Q(d_ff_1_q));  // open: Qn, preset, en, reset
  D_Flip_Flop d_ff_2 (.clk(clock_1_out), .D(nextstate_1_s1next), .Q(d_ff_2_q));  // open: Qn, preset, en, reset
endmodule
